// Logisim project BQMS.circ as structural Verilog: 1 circuit, main circuit main
module main (
  input  sig,
  input  rst,
  output op
);

  wire clk_out, d_ff_1_q, not_1_out, not_2_out;

  D_Flip_Flop d_ff_1 (.D(sig), .clk(clk_out), .Q(d_ff_1_q), .reset(not_1_out));  // open: Qn, preset
  Clock clk (.out(clk_out));
  not not_1 (not_1_out, rst);
  not not_2 (not_2_out, sig);
  and and_1 (op, not_2_out, d_ff_1_q);
endmodule
